// Logisim project buttons.circ as structural Verilog: 1 circuit, main circuit snes_buttons
module snes_buttons (
  output start_button,
  output select_button,
  output left_button
);


  assign left_button = 1'b0;
  assign select_button = 1'b1;
  assign start_button = 1'b1;
endmodule
