// Logisim project snazzy.circ as structural Verilog: 7 circuits, main circuit main
module main (
  input  in_1,
  input  in_2,
  input  in_3,
  input  in_4,
  input  in_5,
  input  C_left,
  input  C_select,
  input  C_start,
  input  SNES_latch,
  output SNES_data1
);

  wire SNES_clock_out;

  Clock SNES_clock (.out(SNES_clock_out));
  CD4021B cd4021b_1 (
    .Q8(SNES_data1), .CL(SNES_clock_out), .PSC(SNES_latch), .P1(C_start), .P2(C_select), .P3(C_left),
    .P4(in_5), .P5(in_4), .P6(in_3), .P7(in_2), .P8(in_1));  // open: Q6, Q7, SI
  // Digital_Oscilloscope digital_oscilloscope_1: pin names not known; wires that end beside it: SNES_clock_out, SNES_latch, SNES_data1

  // Notes on the sheet:
  //   clock
  //   SNES_latch
  //   SNES_data1
endmodule

module CD4021B_dff (
  input  CL,
  input  P,
  input  nD,
  input  PS,
  output nQ
);

  wire nCL, not_1_out, not_3_out, transmission_1_p4, transmission_3_p4, transmission_4_p4, transmission_5_p4,
       transmission_6_p4;

  not not_1 (not_1_out, PS);
  // Transmission_Gate transmission_1: pin names not known; wires that end beside it: P, PS, not_1_out, transmission_1_p4
  // Transmission_Gate transmission_2: pin names not known; wires that end beside it: nD, not_1_out, PS, transmission_1_p4
  // Transmission_Gate transmission_3: pin names not known; wires that end beside it: transmission_1_p4, CL, nCL, transmission_3_p4
  not not_2 (nCL, CL);
  not not_3 (not_3_out, transmission_3_p4);
  // Transmission_Gate transmission_4: pin names not known; wires that end beside it: transmission_3_p4, nCL, CL, transmission_4_p4
  not not_4 (transmission_4_p4, not_3_out);
  // Transmission_Gate transmission_5: pin names not known; wires that end beside it: not_3_out, nCL, CL, transmission_5_p4
  // Transmission_Gate transmission_6: pin names not known; wires that end beside it: transmission_5_p4, CL, nCL, transmission_6_p4
  not not_5 (transmission_6_p4, nQ);
  not not_6 (nQ, transmission_5_p4);
endmodule

module CD4021B (
  input  P1,
  input  P2,
  input  P3,
  input  P4,
  input  P5,
  input  P6,
  input  P7,
  input  P8,
  input  SI,
  input  CL,
  input  PSC,
  output Q6,
  output Q7,
  output Q8
);

  wire cd4021b_dff_simple_1_nq, cd4021b_dff_simple_2_nq, cd4021b_dff_simple_3_nq, cd4021b_dff_simple_4_nq,
       cd4021b_dff_simple_5_nq, cd4021b_dff_simple_6_nq, cd4021b_dff_simple_7_nq, cd4021b_dff_simple_8_nq,
       nand_1_out, not_1_out, not_2_out, not_3_out, not_4_out, not_5_out, not_6_out, not_7_out, not_8_out,
       not_9_out, not_10_out, not_11_out, not_13_out, not_14_out;

  not not_1 (not_1_out, SI);
  not not_2 (not_2_out, PSC);
  not not_3 (not_3_out, not_1_out);
  not not_4 (not_4_out, not_3_out);
  not not_5 (not_5_out, CL);
  nand nand_1 (nand_1_out, not_5_out, not_2_out);
  not not_6 (not_6_out, P1);
  // Probe on cd4021b_dff_simple_1_nq
  not not_7 (not_7_out, P2);
  CD4021B_dff_simple cd4021b_dff_simple_1 (
    .nQ(cd4021b_dff_simple_1_nq), .P(not_6_out), .PS(not_2_out), .nD(not_4_out), .CL(nand_1_out));
  // Probe on cd4021b_dff_simple_2_nq
  CD4021B_dff_simple cd4021b_dff_simple_2 (
    .nQ(cd4021b_dff_simple_2_nq), .P(not_7_out), .PS(not_2_out), .nD(cd4021b_dff_simple_1_nq), .CL(nand_1_out));
  // Probe on cd4021b_dff_simple_3_nq
  not not_8 (not_8_out, P3);
  CD4021B_dff_simple cd4021b_dff_simple_3 (
    .nQ(cd4021b_dff_simple_3_nq), .P(not_8_out), .PS(not_2_out), .nD(cd4021b_dff_simple_2_nq), .CL(nand_1_out));
  // Probe on cd4021b_dff_simple_4_nq
  not not_9 (not_9_out, P4);
  CD4021B_dff_simple cd4021b_dff_simple_4 (
    .nQ(cd4021b_dff_simple_4_nq), .P(not_9_out), .PS(not_2_out), .nD(cd4021b_dff_simple_3_nq), .CL(nand_1_out));
  // Probe on cd4021b_dff_simple_5_nq
  not not_10 (not_10_out, P5);
  CD4021B_dff_simple cd4021b_dff_simple_5 (
    .nQ(cd4021b_dff_simple_5_nq), .P(not_10_out), .PS(not_2_out), .nD(cd4021b_dff_simple_4_nq),
    .CL(nand_1_out));
  // Probe on cd4021b_dff_simple_6_nq
  not not_11 (not_11_out, P6);
  CD4021B_dff_simple cd4021b_dff_simple_6 (
    .nQ(cd4021b_dff_simple_6_nq), .P(not_11_out), .PS(not_2_out), .nD(cd4021b_dff_simple_5_nq),
    .CL(nand_1_out));
  not not_12 (Q6, cd4021b_dff_simple_6_nq);
  not not_13 (not_13_out, P7);
  CD4021B_dff_simple cd4021b_dff_simple_7 (
    .nQ(cd4021b_dff_simple_7_nq), .P(not_13_out), .PS(not_2_out), .nD(cd4021b_dff_simple_6_nq),
    .CL(nand_1_out));
  // Probe on cd4021b_dff_simple_7_nq
  not not_14 (not_14_out, P8);
  not not_15 (Q7, cd4021b_dff_simple_7_nq);
  // Probe on cd4021b_dff_simple_8_nq
  CD4021B_dff_simple cd4021b_dff_simple_8 (
    .nQ(cd4021b_dff_simple_8_nq), .P(not_14_out), .PS(not_2_out), .nD(cd4021b_dff_simple_7_nq),
    .CL(nand_1_out));
  not not_16 (Q8, cd4021b_dff_simple_8_nq);
endmodule

module CD4021B_dff_simple (
  input  P,
  input  PS,
  input  nD,
  input  CL,
  output nQ
);

  wire and_1_out, and_2_out, d_ff_1_q, not_1_out, not_2_out, not_3_out;

  not not_1 (not_1_out, PS);
  not not_2 (not_2_out, P);
  and and_1 (and_1_out, P, not_1_out);
  D_Flip_Flop d_ff_1 (.D(not_3_out), .clk(CL), .Q(d_ff_1_q), .Qn(nQ), .preset(and_1_out), .reset(and_2_out));
  not not_3 (not_3_out, nD);
  and and_2 (and_2_out, not_2_out, not_1_out);
  // NoConnect on d_ff_1_q
endmodule

module CD4021B_dff2 (
  input  CL,
  input  P,
  input  nD,
  input  PS,
  output nQ
);

  wire nCL, not_1_out, not_4_out, transmission_1_p4, transmission_2_p4, transmission_4_p4, transmission_5_p4,
       transmission_6_p4;

  not not_1 (not_1_out, PS);
  // Transmission_Gate transmission_1: pin names not known; wires that end beside it: P, PS, not_1_out, transmission_1_p4
  // Transmission_Gate transmission_2: pin names not known; wires that end beside it: nD, CL, nCL, transmission_2_p4
  // Transmission_Gate transmission_3: pin names not known; wires that end beside it: transmission_2_p4, not_1_out, PS, transmission_1_p4
  // Transmission_Gate transmission_4: pin names not known; wires that end beside it: transmission_2_p4, nCL, CL, transmission_4_p4
  not not_2 (nCL, CL);
  not not_3 (transmission_4_p4, not_4_out);
  not not_4 (not_4_out, transmission_1_p4);
  // Transmission_Gate transmission_5: pin names not known; wires that end beside it: not_4_out, nCL, CL, transmission_5_p4
  not not_5 (nQ, transmission_5_p4);
  // Transmission_Gate transmission_6: pin names not known; wires that end beside it: transmission_5_p4, CL, nCL, transmission_6_p4
  not not_6 (transmission_6_p4, nQ);
endmodule

module MC14021B (
  input  P1,
  input  in_2,
  input  in_3,
  input  in_4,
  input  in_5,
  input  in_6,
  input  in_7,
  input  in_8,
  input  PS,
  input  DS,
  input  CLOCK,
  output Q6,
  output Q7,
  output Q8
);

  wire mc14021b_dff_1_q, mc14021b_dff_2_q, mc14021b_dff_3_q, mc14021b_dff_4_q, mc14021b_dff_5_q,
       mc14021b_dff_6_nq, mc14021b_dff_6_q, mc14021b_dff_7_nq, mc14021b_dff_7_q, mc14021b_dff_8_nq,
       mc14021b_dff_8_q, nand_1_out, not_1_out, not_2_out, not_3_out, not_4_out, not_5_out;

  not not_1 (not_1_out, PS);
  not not_2 (not_2_out, not_1_out);
  not not_3 (not_3_out, DS);
  not not_4 (not_4_out, not_3_out);
  not not_5 (not_5_out, CLOCK);
  nand nand_1 (nand_1_out, not_1_out, not_5_out);
  MC14021B_dff mc14021b_dff_1 (
    .Q(mc14021b_dff_1_q), .P(P1), .PS(not_2_out), .D(not_4_out), .CLOCK(nand_1_out));  // open: nQ
  MC14021B_dff mc14021b_dff_2 (
    .Q(mc14021b_dff_2_q), .P(in_2), .PS(not_2_out), .D(mc14021b_dff_1_q), .CLOCK(nand_1_out));  // open: nQ
  MC14021B_dff mc14021b_dff_3 (
    .Q(mc14021b_dff_3_q), .P(in_3), .PS(not_2_out), .D(mc14021b_dff_2_q), .CLOCK(nand_1_out));  // open: nQ
  MC14021B_dff mc14021b_dff_4 (
    .Q(mc14021b_dff_4_q), .P(in_4), .PS(not_2_out), .D(mc14021b_dff_3_q), .CLOCK(nand_1_out));  // open: nQ
  MC14021B_dff mc14021b_dff_5 (
    .Q(mc14021b_dff_5_q), .P(in_5), .PS(not_2_out), .D(mc14021b_dff_4_q), .CLOCK(nand_1_out));  // open: nQ
  MC14021B_dff mc14021b_dff_6 (
    .Q(mc14021b_dff_6_q), .nQ(mc14021b_dff_6_nq), .P(in_6), .PS(not_2_out), .D(mc14021b_dff_5_q),
    .CLOCK(nand_1_out));
  not not_6 (Q6, mc14021b_dff_6_nq);
  MC14021B_dff mc14021b_dff_7 (
    .Q(mc14021b_dff_7_q), .nQ(mc14021b_dff_7_nq), .P(in_7), .PS(not_2_out), .D(mc14021b_dff_6_q),
    .CLOCK(nand_1_out));
  not not_7 (Q7, mc14021b_dff_7_nq);
  // NoConnect on mc14021b_dff_8_q
  MC14021B_dff mc14021b_dff_8 (
    .Q(mc14021b_dff_8_q), .nQ(mc14021b_dff_8_nq), .P(in_8), .PS(not_2_out), .D(mc14021b_dff_7_q),
    .CLOCK(nand_1_out));
  not not_8 (Q8, mc14021b_dff_8_nq);
endmodule

module MC14021B_dff (
  input  P,
  input  PS,
  input  D,
  input  CLOCK,
  output Q,
  output nQ
);

  wire and_1_out, and_2_out, not_1_out;

  not not_1 (not_1_out, P);
  and and_1 (and_1_out, P, PS);
  D_Flip_Flop d_ff_1 (.D(D), .clk(CLOCK), .Q(Q), .Qn(nQ), .preset(and_1_out), .reset(and_2_out));
  and and_2 (and_2_out, not_1_out, PS);
endmodule
